# Fritzing sketch Untitled Sketch 2 (saved by Fritzing 0.9.4)
circuit board: 8.46667cm x 5.64444cm
breadboards: 1

parts:
  Componente1 = Arduino Mega 2560 (Rev3)
  DI2 = 7-Segment LED Display [package=THT]
  R1 = Resistor [tolerance=±5% resistance=180 package=THT]
  R2 = Resistor [tolerance=±5% resistance=180 package=THT]
  R3 = Resistor [tolerance=±5% resistance=180 package=THT]
  R4 = Resistor [tolerance=±5% resistance=180 package=THT]
  R5 = Resistor [tolerance=±5% resistance=180 package=THT]
  R6 = Resistor [tolerance=±5% resistance=180 package=THT]
  R7 = Resistor [tolerance=±5% resistance=180 package=THT]
  LED1 = smd LED [color="Red (633nm)" package="1206 [SMD]"]
  LED2 = smd LED [color="Red (633nm)" package="1206 [SMD]"]
  LED3 = smd LED [color="Green (555nm)" package="1206 [SMD]"]
  LED4 = smd LED [color="Yellow (595nm)" package="1206 [SMD]"]
  LED5 = smd LED [color="Green (555nm)" package="1206 [SMD]"]
  S1 = Momentary Switch [package=ksa_sealed_tac_switch]
  S2 = Momentary Switch [package=ksa_sealed_tac_switch]
  R8 = Resistor [tolerance=±5% resistance=180 package=THT]
  R9 = Resistor [tolerance=±5% resistance=180 package=THT]  # not connected
  R10 = Resistor [tolerance=±5% resistance=180 package=THT]
  R11 = Resistor [tolerance=±5% resistance=10k package=THT]
  R12 = Resistor [tolerance=±5% resistance=10k package=THT]
  R13 = Resistor [tolerance=±5% resistance=180 package=THT]
  R14 = Resistor [tolerance=±5% resistance=180 package=THT]

nets:
  N1: Componente1.D12_PWM, S1.4, S2.4, R11.Pin_0, R12.Pin_0
  N2: Componente1.D11_PWM, LED1.anode
  N3: Componente1.D10_PWM, LED4.anode
  N4: Componente1.D9_PWM, LED5.anode
  N5: Componente1.D8_PWM, R7.Pin_0
  N6: Componente1.D2_PWM, R5.Pin_1
  N7: Componente1.D3_PWM, R4.Pin_1
  N8: Componente1.D4_PWM, R3.Pin_1
  N9: Componente1.D5_PWM, R1.Pin_0
  N10: Componente1.D6_PWM, R2.Pin_0
  N11: Componente1.D7_PWM, R6.Pin_0
  N12: Componente1.D22, LED2.anode
  N13: Componente1.D24, LED3.anode
  N14: DI2.cathodeE, R2.Pin_1
  N15: DI2.cathodeD, R1.Pin_1
  N16: DI2.commAnode#2, S1.2, S2.2, R8.Pin_1, R10.Pin_1, R11.Pin_1, R12.Pin_1, R13.Pin_1, R14.Pin_1
  N17: DI2.cathodeC, R3.Pin_0
  N18: DI2.cathodeB, R4.Pin_0
  N19: DI2.cathodeA, R5.Pin_0
  N20: DI2.cathodeF, R6.Pin_1
  N21: DI2.cathodeG, R7.Pin_1
  N22: LED1.cathode, R8.Pin_0
  N23: LED2.cathode, R13.Pin_0
  N24: LED3.cathode, R14.Pin_0
  N25: LED5.cathode, R10.Pin_0
